// Logisim project RSC.circ as structural Verilog
module ALU (
  input  [31:0] A,
  input  [31:0] B,
  input  S2,
  input  S1,
  input  S0,
  output [31:0] ALU_Out
);

  wire [31:0] arith_u_1_au_out, logic_u_1_logic_out;

  Arith_U arith_u_1 (.A(A), .B(B), .S1(S1), .S0(S0), .AU_out(arith_u_1_au_out));
  Logic_U logic_u_1 (.A(A), .B(B), .S1(S1), .S0(S0), .Logic_Out(logic_u_1_logic_out));
  Multiplexer #(.width(32), .enable("false")) multiplexer_1 (
    .in0(arith_u_1_au_out), .in1(logic_u_1_logic_out), .out(ALU_Out), .sel(S2));
  // Probe on logic_u_1_logic_out
  // Probe on arith_u_1_au_out
  // Probe on ALU_Out
  // Probe on A

  // Notes on the sheet:
  //   LU
  //   AU
  //   Ahmad Mohammad
  //   ALU Circuit
  //   CLA5
  //   10/15
endmodule

module Logic_U (
  input  [31:0] A,
  input  [31:0] B,
  input  S1,
  input  S0,
  output [31:0] Logic_Out
);

  wire [31:0] and_1_out, not_1_out, or_1_out, shifter_1_out;

  assign and_1_out = A & B;  // AND_Gate and_1, 32 bits wide
  assign or_1_out = A | B;  // OR_Gate or_1, 32 bits wide
  Shifter #(.width(32), .shift("ar")) shifter_1 (.in(A), .\dist (5'b00001), .out(shifter_1_out));
  assign not_1_out = ~A;  // NOT_Gate not_1, 32 bits wide
  // Probe on A
  // Probe on B
  Multiplexer #(.select(2), .width(32), .enable("false")) multiplexer_1 (
    .in0(and_1_out), .in1(or_1_out), .in2(shifter_1_out), .in3(not_1_out), .out(Logic_Out), .sel({S1, S0}));
  // Probe on Logic_Out

  // Notes on the sheet:
  //   Ahmad Mohammad
  //   Logic Unit
  //   CLA5
  //   10/15
endmodule

module Arith_U (
  input  [31:0] A,
  input  [31:0] B,
  input  S1,
  input  S0,
  output [31:0] AU_out
);

  wire and_1_out, not_2_out;
  wire [31:0] adder_1_out, multiplexer_1_out, not_1_out;

  assign not_1_out = ~B;  // NOT_Gate not_1, 32 bits wide
  not not_2 (not_2_out, S0);
  Multiplexer #(.select(2), .width(32), .enable("false")) multiplexer_1 (
    .in0(not_1_out), .in1(B), .in2({32{1'b0}}), .out(multiplexer_1_out), .sel({S1, S0}));  // open: in3
  and and_1 (and_1_out, S1, S0);
  Adder #(.width(32)) adder_1 (.a(A), .b(multiplexer_1_out), .out(adder_1_out), .cin(not_2_out));  // open: cout
  Multiplexer #(.width(32), .enable("false")) multiplexer_2 (.in0(adder_1_out), .in1(B), .out(AU_out), .sel(and_1_out));
  // Probe on AU_out

  // Notes on the sheet:
  //   Arithmetic Unit
  //   CLA4
  //   10/01
  //   Ahmad Mohammad
endmodule

module SC (
  input  clock,
  input  clear,
  output [2:0] SEQ_OIUT
);

  wire and_1_out;
  wire [2:0] j_k_ff_3_q;

  and and_1 (and_1_out, j_k_ff_3_q[1], j_k_ff_3_q[0]);
  J_K_Flip_Flop j_k_ff_1 (
    .J(and_1_out), .clk(clock), .K(and_1_out), .Q(j_k_ff_3_q[2]), .reset(clear));  // open: Qn, preset, en
  J_K_Flip_Flop j_k_ff_2 (
    .J(j_k_ff_3_q[0]), .clk(clock), .K(j_k_ff_3_q[0]), .Q(j_k_ff_3_q[1]), .reset(clear));  // open: Qn, preset, en
  J_K_Flip_Flop j_k_ff_3 (.J(1'b1), .clk(clock), .K(1'b1), .Q(j_k_ff_3_q[0]), .reset(clear));  // open: Qn, preset, en
  Register #(.width(3)) register_1 (.D(j_k_ff_3_q), .Q(SEQ_OIUT), .clk(clock), .clr(clear));  // open: en

  // Notes on the sheet:
  //   Ahmad Mohammad
  //   CLA6 Sequence Counter
endmodule

module RSC (
);

  wire control_1_acc_bus, control_1_acc_clr, control_1_acc_ld, control_1_ar_ld, control_1_dr_bus,
       control_1_dr_ld, control_1_ir_ld, control_1_outr_ld, control_1_pc_bus, control_1_pc_inc,
       control_1_pc_ld, control_1_r_bus, control_1_r_ld, control_1_ram_en, control_1_ram_r_prime_w,
       control_1_z_ld, Primary_Clock_out, z_reg_1_z_out;
  wire [2:0] control_1_alu_sel;
  wire [3:0] control_1_debug_instruction, outr_1_data_out_2, outr_1_data_out_3, outr_1_data_out_4;
  wire [7:0] control_1_t;
  wire [31:0] acc_1_data_out, alu_1_alu_out, AR_data_out, dr_1_data_out, ir_1_data_out, outr_1_data_out,
       r_1_data_out_2;

  Clock Primary_Clock (.out(Primary_Clock_out));
  Hex_Digit_Display hex_digit_display_1 (.value(outr_1_data_out[31:28]));  // open: dp
  Hex_Digit_Display hex_digit_display_2 (.value(outr_1_data_out_4));  // open: dp
  AR AR (.Data_In(r_1_data_out_2), .clock(Primary_Clock_out), .load(control_1_ar_ld), .Data_Out(AR_data_out));
  ALU alu_1 (
    .A(acc_1_data_out), .B(r_1_data_out_2), .S2(control_1_alu_sel[2]), .S1(control_1_alu_sel[1]),
    .S0(control_1_alu_sel[0]), .ALU_Out(alu_1_alu_out));
  Hex_Digit_Display hex_digit_display_3 (.value(outr_1_data_out_3));  // open: dp
  R r_1 (
    .Data_In(r_1_data_out_2), .clock(Primary_Clock_out), .load(control_1_r_ld), .bus(control_1_r_bus),
    .Data_Out_2(r_1_data_out_2));  // open: Data_Out
  OUTR outr_1 (
    .Data_In(r_1_data_out_2), .clock(Primary_Clock_out), .load(control_1_outr_ld),
    .Data_Out({outr_1_data_out[31:28], outr_1_data_out_4, outr_1_data_out_3, outr_1_data_out_2, outr_1_data_out[15:0]}));
  Hex_Digit_Display hex_digit_display_4 (.value(outr_1_data_out_2));  // open: dp
  Hex_Digit_Display hex_digit_display_5 (.value(outr_1_data_out[15:12]));  // open: dp
  DR dr_1 (
    .Data_In(r_1_data_out_2), .clock(Primary_Clock_out), .load(control_1_dr_ld), .bus(control_1_dr_bus),
    .Data_Out(dr_1_data_out), .Bus_Out(r_1_data_out_2));
  Hex_Digit_Display hex_digit_display_6 (.value(outr_1_data_out[11:8]));  // open: dp
  RAM #(.addrWidth(16), .dataWidth(32)) ram_1 (
    .addr(AR_data_out[15:0]), .data(r_1_data_out_2), .sel(control_1_ram_en), .clk(Primary_Clock_out),
    .ld(control_1_ram_r_prime_w));  // open: clr
  PC pc_1 (
    .Data_In(r_1_data_out_2), .clock(Primary_Clock_out), .load(control_1_pc_ld), .bus(control_1_pc_bus),
    .count(control_1_pc_inc), .Bus_Out(r_1_data_out_2));  // open: Data_Out
  IR ir_1 (.Data_In(dr_1_data_out), .clock(Primary_Clock_out), .load(control_1_ir_ld), .Data_Out(ir_1_data_out));
  ACC acc_1 (
    .Data_In(alu_1_alu_out), .clock(Primary_Clock_out), .load(control_1_acc_ld), .bus(control_1_acc_bus),
    .clear(control_1_acc_clr), .Data_Out(acc_1_data_out), .Bus_Out(r_1_data_out_2));
  Hex_Digit_Display hex_digit_display_7 (.value(outr_1_data_out[7:4]));  // open: dp
  Z_Reg z_reg_1 (.ACC_in(acc_1_data_out), .Clock(Primary_Clock_out), .Load(control_1_z_ld), .Z_Out(z_reg_1_z_out));
  Hex_Digit_Display hex_digit_display_8 (.value(outr_1_data_out[3:0]));  // open: dp
  Control control_1 (
    .RAM_R_prime_W(control_1_ram_r_prime_w), .RAM_EN(control_1_ram_en), .AR_LD(control_1_ar_ld),
    .PC_BUS(control_1_pc_bus), .PC_INC(control_1_pc_inc), .PC_LD(control_1_pc_ld), .DR_BUS(control_1_dr_bus),
    .DR_LD(control_1_dr_ld), .R_BUS(control_1_r_bus), .R_LD(control_1_r_ld), .ACC_BUS(control_1_acc_bus),
    .ACC_CLR(control_1_acc_clr), .ACC_LD(control_1_acc_ld), .ALU_SEL(control_1_alu_sel),
    .OUTR_LD(control_1_outr_ld), .Z_LD(control_1_z_ld), .IR_LD(control_1_ir_ld), .Clock(Primary_Clock_out),
    .Z_In(z_reg_1_z_out), .T(control_1_t), .IR_In(ir_1_data_out),
    .Debug_Instruction(control_1_debug_instruction));
  // Probe on control_1_t
  // Probe on control_1_debug_instruction

  // Notes on the sheet:
  //   Ahmad Mohammad
  //   RSC
endmodule

// DECODER
module Decoder (
  input  [31:0] IR_In,
  output [15:0] D_out,
  output [3:0] Debug_Instruction
);

  wire or_1_out;
  wire [3:0] or_2_out;
  wire [15:0] decoder_1_out0;

  Multiplexer #(.width(16), .enable("false")) multiplexer_1 (
    .in0(decoder_1_out0), .in1({16{1'b0}}), .out(D_out), .sel(or_1_out));
  or or_1 (or_1_out, or_2_out[0], or_2_out[1], or_2_out[2], or_2_out[3]);
  Decoder_part #(.select(4), .enable("false")) decoder_1 (
    .out0(decoder_1_out0[0]), .out1(decoder_1_out0[1]), .out2(decoder_1_out0[2]), .out3(decoder_1_out0[3]),
    .out4(decoder_1_out0[4]), .out5(decoder_1_out0[5]), .out6(decoder_1_out0[6]), .out7(decoder_1_out0[7]),
    .out8(decoder_1_out0[8]), .out9(decoder_1_out0[9]), .out10(decoder_1_out0[10]),
    .out11(decoder_1_out0[11]), .out12(decoder_1_out0[12]), .out13(decoder_1_out0[13]),
    .out14(decoder_1_out0[14]), .out15(decoder_1_out0[15]), .sel(IR_In[3:0]));
  assign or_2_out = IR_In[7:4] | IR_In[11:8] | IR_In[15:12] | IR_In[19:16] | IR_In[23:20] | IR_In[27:24] | IR_In[31:28];  // OR_Gate or_2, 4 bits wide

  assign Debug_Instruction = IR_In[3:0];

  // Notes on the sheet:
  //   Ahmad Mohammad
  //   CLA7 Decoder
endmodule

// TIMER
module Timer (
  input  Stop,
  input  Clear,
  input  Clock,
  output [7:0] T_Out
);

  wire [2:0] sc_1_seq_oiut;
  wire [7:0] decoder_1_out0;

  Multiplexer #(.width(8), .enable("false")) multiplexer_1 (
    .in0(decoder_1_out0), .in1({8{1'b0}}), .out(T_Out), .sel(Stop));
  Decoder_part #(.select(3), .enable("false")) decoder_1 (
    .out0(decoder_1_out0[0]), .out1(decoder_1_out0[1]), .out2(decoder_1_out0[2]), .out3(decoder_1_out0[3]),
    .out4(decoder_1_out0[4]), .out5(decoder_1_out0[5]), .out6(decoder_1_out0[6]), .out7(decoder_1_out0[7]),
    .sel(sc_1_seq_oiut));
  SC sc_1 (.clock(Clock), .clear(Clear), .SEQ_OIUT(sc_1_seq_oiut));

  // Notes on the sheet:
  //   Ahmad Mohammad
  //   CLA7 TIMER
endmodule

// Z
module Z_Reg (
  input  Clock,
  input  [31:0] ACC_in,
  input  Load,
  output Z_Out
);

  wire multiplexer_1_out, or_2_out;
  wire [3:0] or_1_out;

  assign or_1_out = ACC_in[3:0] | ACC_in[7:4] | ACC_in[11:8] | ACC_in[15:12] | ACC_in[19:16] | ACC_in[23:20] | ACC_in[27:24] | ACC_in[31:28];  // OR_Gate or_1, 4 bits wide
  or or_2 (or_2_out, or_1_out[0], or_1_out[1], or_1_out[2], or_1_out[3]);
  Multiplexer #(.enable("false")) multiplexer_1 (.in0(1'b1), .in1(1'b0), .out(multiplexer_1_out), .sel(or_2_out));
  _1bit_reg u_1bit_reg_1 (.Data(multiplexer_1_out), .Clock(Clock), .Load(Load), .Data_out(Z_Out));  // open: clear

  // Notes on the sheet:
  //   Ahmad Mohammad
  //   Z REGISTER
endmodule

module _1bit_reg (
  input  Clock,
  input  Data,
  input  Load,
  input  clear,
  output Data_out
);

  wire and_1_out, and_2_out, not_1_out, not_2_out;

  and and_1 (and_1_out, Data, Load);
  not not_1 (not_1_out, Data);
  and and_2 (and_2_out, not_1_out, Load);
  J_K_Flip_Flop j_k_ff_1 (
    .J(and_1_out), .clk(Clock), .K(and_2_out), .Q(Data_out), .preset(1'b0), .en(not_2_out), .reset(clear));  // open: Qn
  not not_2 (not_2_out, clear);
endmodule

module Control (
  input  Clock,
  input  Z_In,
  input  [31:0] IR_In,
  output IR_LD,
  output RAM_R_prime_W,
  output RAM_EN,
  output AR_LD,
  output [7:0] T,
  output PC_BUS,
  output PC_INC,
  output PC_LD,
  output DR_BUS,
  output DR_LD,
  output R_BUS,
  output R_LD,
  output ACC_BUS,
  output [3:0] Debug_Instruction,
  output ACC_CLR,
  output ACC_LD,
  output [2:0] ALU_SEL,
  output OUTR_LD,
  output Z_LD
);

  wire s_ld_1_s_ld, S_Reg_data_out, sc_clr_1_sc_clr;
  wire [15:0] decoder_1_d_out;

  IR_LD ir_ld_1 (.t2(T[2]), .clock(Clock), .IR_LD(IR_LD));
  RAM_RW ram_rw_1 (
    .t1(T[1]), .t3(T[3]), .t5(T[5]), .d1(decoder_1_d_out[1]), .d2(decoder_1_d_out[2]),
    .d5(decoder_1_d_out[5]), .d6(decoder_1_d_out[6]), .z(Z_In), .RAM_RW(RAM_R_prime_W));
  RAM_EN ram_en_1 (
    .t1(T[1]), .t3(T[3]), .t5(T[5]), .t6(T[6]), .d1(decoder_1_d_out[1]), .d2(decoder_1_d_out[2]),
    .d5(decoder_1_d_out[5]), .d6(decoder_1_d_out[6]), .z(Z_In), .RAM_EN(RAM_EN));
  AR_LD ar_ld_1 (
    .t0(T[0]), .t2(T[2]), .t4(T[4]), .clock(Clock), .d1(decoder_1_d_out[1]), .d2(decoder_1_d_out[2]),
    .AR_LD(AR_LD));
  PC_Bus pc_bus_1 (.t0(T[0]), .t2(T[2]), .PC_Bus(PC_BUS));
  PC_INC pc_inc_1 (
    .t1(T[1]), .t3(T[3]), .clock(Clock), .d1(decoder_1_d_out[1]), .d2(decoder_1_d_out[2]),
    .d6(decoder_1_d_out[6]), .z(Z_In), .PC_INC(PC_INC));
  PC_LD pc_ld_1 (.t4(T[4]), .clock(Clock), .d5(decoder_1_d_out[5]), .d6(decoder_1_d_out[6]), .z(Z_In), .PC_LD(PC_LD));
  DR_BUS dr_bus_1 (
    .t4(T[4]), .t6(T[6]), .d1(decoder_1_d_out[1]), .d2(decoder_1_d_out[2]), .d5(decoder_1_d_out[5]),
    .d6(decoder_1_d_out[6]), .z(Z_In), .DR_BUS(DR_BUS));
  DR_LD dr_ld_1 (
    .t1(T[1]), .t3(T[3]), .t5(T[5]), .clock(Clock), .d1(decoder_1_d_out[1]), .d2(decoder_1_d_out[2]),
    .d5(decoder_1_d_out[5]), .d6(decoder_1_d_out[6]), .z(Z_In), .DR_LD(DR_LD));
  R_BUS r_bus_1 (
    .t3(T[3]), .d4(decoder_1_d_out[4]), .d8(decoder_1_d_out[8]), .d9(decoder_1_d_out[9]),
    .d12(decoder_1_d_out[12]), .d13(decoder_1_d_out[13]), .R_BUS(R_BUS));
  R_LD r_ld_1 (.t3(T[3]), .clock(Clock), .d3(decoder_1_d_out[3]), .R_LD(R_LD));
  ACC_BUS acc_bus_1 (
    .t3(T[3]), .t5(T[5]), .d2(decoder_1_d_out[2]), .d3(decoder_1_d_out[3]), .d7(decoder_1_d_out[7]),
    .ACC_BUS(ACC_BUS));
  ACC_CLR acc_clr_1 (.t3(T[3]), .d11(decoder_1_d_out[11]), .ACC_CLR(ACC_CLR));
  ACC_LD acc_ld_1 (
    .t3(T[3]), .t6(T[6]), .clock(Clock), .d1(decoder_1_d_out[1]), .d4(decoder_1_d_out[4]),
    .d8(decoder_1_d_out[8]), .d9(decoder_1_d_out[9]), .d10(decoder_1_d_out[10]), .d12(decoder_1_d_out[12]),
    .d13(decoder_1_d_out[13]), .d14(decoder_1_d_out[14]), .d15(decoder_1_d_out[15]), .ACC_LD(ACC_LD));
  ALU_SEL alu_sel_1 (
    .d1(decoder_1_d_out[1]), .d4(decoder_1_d_out[4]), .d9(decoder_1_d_out[9]), .d10(decoder_1_d_out[10]),
    .d12(decoder_1_d_out[12]), .d13(decoder_1_d_out[13]), .d14(decoder_1_d_out[14]),
    .d15(decoder_1_d_out[15]), .S0(ALU_SEL[0]), .S1(ALU_SEL[1]), .S2(ALU_SEL[2]));
  OUTR_LD outr_ld_1 (.t3(T[3]), .clock(Clock), .d7(decoder_1_d_out[7]), .OUTR_LD(OUTR_LD));
  Z_LD z_ld_1 (.Z_LD(Z_LD));
  Timer timer_1 (.T_Out(T), .Stop(S_Reg_data_out), .Clock(Clock), .Clear(sc_clr_1_sc_clr));
  _1bit_reg S_Reg (.Data(1'b1), .Clock(Clock), .Load(s_ld_1_s_ld), .Data_out(S_Reg_data_out));  // open: clear
  S_LD s_ld_1 (.t3(T[3]), .clock(Clock), .d0(decoder_1_d_out[0]), .S_LD(s_ld_1_s_ld));
  SC_CLR sc_clr_1 (
    .t4(T[4]), .t5(T[5]), .t7(T[7]), .d1(decoder_1_d_out[1]), .d2(decoder_1_d_out[2]),
    .d5(decoder_1_d_out[5]), .d6(decoder_1_d_out[6]), .z(Z_In), .SC_CLR(sc_clr_1_sc_clr));
  Decoder decoder_1 (.D_out(decoder_1_d_out), .Debug_Instruction(Debug_Instruction), .IR_In(IR_In));

  // Notes on the sheet:
  //   Ahmad Mohammad
  //   Control Unit
endmodule
