// Logisim project custom_reg.circ as structural Verilog: 12 circuits, main circuit 1bit_reg
module _1bit_reg (
  input  Clock,
  input  Data,
  input  Clear,
  input  Load,
  output Data_out
);

  wire and_1_out, and_2_out, not_1_out, not_2_out;

  and and_1 (and_1_out, Data, Load);
  not not_1 (not_1_out, Data);
  and and_2 (and_2_out, not_1_out, Load);
  J_K_Flip_Flop j_k_ff_1 (
    .J(and_1_out), .clk(Clock), .K(and_2_out), .Q(Data_out), .preset(1'b0), .en(not_2_out), .reset(Clear));  // open: Qn
  not not_2 (not_2_out, Clear);

  // Notes on the sheet:
  //   Anthony Davis
  //   CLA 5
  //   1bit_reg
endmodule

module Register (
  input  [31:0] Data_In,
  input  clock,
  input  load,
  output [31:0] Data_out
);

  Register_part #(.width(32)) register_1 (.D(Data_In), .en(load), .Q(Data_out), .clk(clock));  // open: clr

  // Notes on the sheet:
  //   Ahmad Mohammad
  //   OLA 5
  //   Register Circuit
endmodule

module BusRegister (
  input  [31:0] Data_In,
  input  clock,
  input  load,
  input  Bus,
  output [31:0] Data_out,
  output [31:0] Bus_Out
);

  Register_part #(.width(32)) register_1 (.D(Data_In), .en(load), .Q(Data_out), .clk(clock));  // open: clr
  assign Bus_Out = Bus ? Data_out : 32'bz;  // Controlled_Buffer controlled_buffer_1

  // Notes on the sheet:
  //   Ahmad Mohammad
  //   OLA5
  //   Bus Register
endmodule

module ClearRegister (
  input  [31:0] Data_In,
  input  clock,
  input  load,
  input  bus,
  input  clear,
  output [31:0] Data_Out,
  output [31:0] Bus_Out
);

  Register_part #(.width(32)) register_1 (.D(Data_In), .en(load), .Q(Data_Out), .clk(clock), .clr(clear));
  assign Bus_Out = bus ? Data_Out : 32'bz;  // Controlled_Buffer controlled_buffer_1
endmodule

module CountRegister (
  input  [31:0] Data_In,
  input  clock,
  input  load,
  input  bus,
  input  count,
  output [31:0] Data_Out,
  output [31:0] Bus_Out
);

  wire or_1_out;
  wire [31:0] adder_1_out, multiplexer_1_out;

  Multiplexer #(.width(32), .enable("false")) multiplexer_1 (
    .in0(Data_In), .in1(adder_1_out), .out(multiplexer_1_out), .sel(count));
  Adder #(.width(32)) adder_1 (.a(Data_Out), .b(32'h1), .out(adder_1_out));  // open: cin, cout
  or or_1 (or_1_out, load, count);
  Register_part #(.width(32)) register_1 (
    .D(multiplexer_1_out), .en(or_1_out), .Q(Data_Out), .clk(clock));  // open: clr
  assign Bus_Out = bus ? Data_Out : 32'bz;  // Controlled_Buffer controlled_buffer_1
endmodule

module ACC (
  input  [31:0] Data_In,
  input  clock,
  input  load,
  input  bus,
  input  clear,
  output [31:0] Data_Out,
  output [31:0] Bus_Out
);

  ClearRegister clearregister_1 (
    .Data_In(Data_In), .clock(clock), .load(load), .bus(bus), .clear(clear), .Data_Out(Data_Out),
    .Bus_Out(Bus_Out));
endmodule

module AR (
  input  [31:0] Data_In,
  input  clock,
  input  load,
  output [31:0] Data_Out
);

  Register register_1 (.Data_In(Data_In), .clock(clock), .load(load), .Data_out(Data_Out));
endmodule

module DR (
  input  [31:0] Data_In,
  input  clock,
  input  load,
  input  bus,
  output [31:0] Data_Out,
  output [31:0] Bus_Out
);

  BusRegister busregister_1 (
    .Data_In(Data_In), .clock(clock), .load(load), .Bus(bus), .Data_out(Data_Out), .Bus_Out(Bus_Out));
endmodule

module IR (
  input  [31:0] Data_In,
  input  clock,
  input  load,
  output [31:0] Data_Out
);

  Register register_1 (.Data_In(Data_In), .clock(clock), .load(load), .Data_out(Data_Out));
endmodule

module OUTR (
  input  [31:0] Data_In,
  input  clock,
  input  load,
  output [31:0] Data_Out
);

  Register register_1 (.Data_In(Data_In), .clock(clock), .load(load), .Data_out(Data_Out));
endmodule

module PC (
  input  [31:0] Data_In,
  input  clock,
  input  load,
  input  bus,
  input  count,
  output [31:0] Data_Out,
  output [31:0] Bus_Out
);

  CountRegister countregister_1 (
    .Data_In(Data_In), .clock(clock), .load(load), .bus(bus), .count(count), .Data_Out(Data_Out),
    .Bus_Out(Bus_Out));
endmodule

module R (
  input  [31:0] Data_In,
  input  clock,
  input  load,
  input  bus,
  output [31:0] Data_Out,
  output [31:0] Data_Out_2
);

  BusRegister busregister_1 (
    .Data_In(Data_In), .clock(clock), .load(load), .Bus(bus), .Data_out(Data_Out), .Bus_Out(Data_Out_2));
endmodule
