// Logisim project mod_counter.circ as structural Verilog: 2 circuits, main circuit Mod9
module Mod9 (
  input  CLOCK,
  output [3:0] Output
);

  wire and_1_out, and_2_out, and_3_out, j_k_ff_1_qn, j_k_ff_2_qn, j_k_ff_3_qn, j_k_ff_4_qn, or_1_out;

  and and_1 (and_1_out, Output[0], Output[1], j_k_ff_2_qn);
  or or_1 (or_1_out, j_k_ff_3_qn, j_k_ff_4_qn);
  and and_2 (and_2_out, j_k_ff_2_qn, Output[0]);
  and and_3 (and_3_out, j_k_ff_1_qn, j_k_ff_2_qn);
  J_K_Flip_Flop j_k_ff_1 (
    .J(and_1_out), .clk(CLOCK), .K(1'b1), .Q(Output[3]), .Qn(j_k_ff_1_qn), .en(1'b1));  // open: preset, reset
  J_K_Flip_Flop j_k_ff_2 (
    .J(or_1_out), .clk(CLOCK), .K(1'b1), .Q(Output[2]), .Qn(j_k_ff_2_qn), .en(1'b1));  // open: preset, reset
  J_K_Flip_Flop j_k_ff_3 (
    .J(and_2_out), .clk(CLOCK), .K(and_2_out), .Q(Output[1]), .Qn(j_k_ff_3_qn), .en(1'b1));  // open: preset, reset
  J_K_Flip_Flop j_k_ff_4 (
    .J(and_3_out), .clk(CLOCK), .K(j_k_ff_2_qn), .Q(Output[0]), .Qn(j_k_ff_4_qn), .en(1'b1));  // open: preset, reset

  // Notes on the sheet:
  //   Ahmad Mohammad
  //   OLA 4
  //   10/06/2021
  //   SEQ CIRCUIT EQU == Q(t+1) = Q(t) + 5
endmodule

module Display (
);

  wire clock_1_out, n7segdecoder_1__1, n7segdecoder_1__2, n7segdecoder_1__3, n7segdecoder_1__4,
       n7segdecoder_1__5, n7segdecoder_1__6, n7segdecoder_1__7;
  wire [3:0] mod9_1_output;

  Clock clock_1 (.out(clock_1_out));
  Mod9 mod9_1 (.CLOCK(clock_1_out), .Output(mod9_1_output));
  _7SegDecoder u_7segdecoder_1 (
    .BCD_In(mod9_1_output), ._1(n7segdecoder_1__1), ._2(n7segdecoder_1__2), ._3(n7segdecoder_1__3),
    ._4(n7segdecoder_1__4), ._5(n7segdecoder_1__5), ._6(n7segdecoder_1__6), ._7(n7segdecoder_1__7));  // open: DP_In, DP_Out
  _7_Segment_Display u_7_segment_display_1 (
    .g(n7segdecoder_1__7), .f(n7segdecoder_1__6), .a(n7segdecoder_1__1), .b(n7segdecoder_1__2),
    .e(n7segdecoder_1__5), .d(n7segdecoder_1__4), .c(n7segdecoder_1__3));  // open: dp

  // Notes on the sheet:
  //   Ahmad Mohammad
  //   10/06/2021
  //   OLA 4 Mod9 display
endmodule
