// Logisim project seven_seg.circ as structural Verilog: 3 circuits, main circuit Display
module Display (
  input  [3:0] BCD,
  input  DP
);

  wire n7segdecoder_1__1, n7segdecoder_1__2, n7segdecoder_1__3, n7segdecoder_1__4, n7segdecoder_1__5,
       n7segdecoder_1__6, n7segdecoder_1__7, n7segdecoder_1_dp_out;

  _7SegDecoder u_7segdecoder_1 (
    .BCD_In(BCD), .DP_In(DP), ._1(n7segdecoder_1__1), ._2(n7segdecoder_1__2), ._3(n7segdecoder_1__3),
    ._4(n7segdecoder_1__4), ._5(n7segdecoder_1__5), ._6(n7segdecoder_1__6), ._7(n7segdecoder_1__7),
    .DP_Out(n7segdecoder_1_dp_out));
  _7_Segment_Display u_7_segment_display_1 (
    .g(n7segdecoder_1__7), .f(n7segdecoder_1__6), .a(n7segdecoder_1__1), .b(n7segdecoder_1__2),
    .e(n7segdecoder_1__5), .d(n7segdecoder_1__4), .c(n7segdecoder_1__3), .dp(n7segdecoder_1_dp_out));

  // Notes on the sheet:
  //   Display
  //   Ahmad Mohammad
  //   09/24/2021
endmodule

module _7SegDecoder (
  input  [3:0] BCD_In,
  input  DP_In,
  output _1,
  output _2,
  output _3,
  output _4,
  output _5,
  output _6,
  output _7,
  output DP_Out
);

  _7segPLD u_7segpld_1 (
    .D(BCD_In[3]), .C(BCD_In[2]), .B(BCD_In[1]), .A(BCD_In[0]), .a_2(_1), .b_2(_2), .c_2(_3), .d_2(_4),
    .e(_5), .f(_6), .g(_7));

  assign DP_Out = DP_In;

  // Notes on the sheet:
  //   Ahmad Mohammad
  //   7 segment decoder CLA 3
  //   09/24
endmodule

module _7segPLD (
  input  D,
  input  C,
  input  B,
  input  A,
  output a_2,
  output b_2,
  output c_2,
  output d_2,
  output e,
  output f,
  output g
);

  wire and_1_out, and_2_out, and_3_out, and_4_out, and_5_out, and_6_out, and_7_out, and_8_out, and_9_out,
       and_10_out, and_11_out, and_12_out, and_13_out, and_14_out, and_15_out, and_16_out, and_17_out,
       and_18_out, and_19_out, and_20_out, and_21_out, and_22_out, and_23_out, and_24_out, and_25_out,
       not_1_out, not_2_out, not_3_out, not_4_out, not_5_out, not_6_out, not_7_out, not_8_out, not_9_out,
       not_10_out, not_11_out, not_12_out, not_13_out, not_14_out, not_15_out, not_16_out, not_17_out,
       not_18_out, not_19_out, not_20_out, not_21_out, not_22_out, not_23_out, not_24_out, not_25_out,
       not_26_out, not_27_out, not_28_out, not_29_out, not_30_out, not_31_out, not_32_out, not_33_out,
       not_34_out, not_35_out;

  not not_1 (not_1_out, C);
  and and_1 (and_1_out, not_1_out, not_2_out);
  not not_2 (not_2_out, A);
  not not_3 (not_3_out, C);
  and and_2 (and_2_out, not_3_out, B);
  and and_3 (and_3_out, C, A);
  not not_4 (not_4_out, D);
  not not_5 (not_5_out, C);
  and and_4 (and_4_out, not_4_out, not_5_out, not_6_out);
  not not_6 (not_6_out, A);
  not not_7 (not_7_out, D);
  and and_5 (and_5_out, not_7_out, not_8_out, not_9_out);
  not not_8 (not_8_out, B);
  not not_9 (not_9_out, A);
  not not_10 (not_10_out, D);
  and and_6 (and_6_out, not_10_out, B, A);
  and and_7 (and_7_out, D, not_11_out, not_12_out);
  not not_11 (not_11_out, C);
  not not_12 (not_12_out, B);
  not not_13 (not_13_out, D);
  and and_8 (and_8_out, not_13_out, not_14_out, not_15_out);
  not not_14 (not_14_out, B);
  not not_15 (not_15_out, A);
  not not_16 (not_16_out, D);
  and and_9 (and_9_out, not_16_out, B, A);
  not not_17 (not_17_out, D);
  and and_10 (and_10_out, not_17_out, C);
  and and_11 (and_11_out, D, not_18_out, not_19_out);
  not not_18 (not_18_out, C);
  not not_19 (not_19_out, B);
  not not_20 (not_20_out, C);
  and and_12 (and_12_out, not_20_out, not_21_out);
  not not_21 (not_21_out, A);
  not not_22 (not_22_out, C);
  and and_13 (and_13_out, not_22_out, B);
  and and_14 (and_14_out, B, not_23_out);
  not not_23 (not_23_out, A);
  not not_24 (not_24_out, B);
  and and_15 (and_15_out, C, not_24_out, A);
  and and_16 (and_16_out, D, C);
  not not_25 (not_25_out, D);
  and and_17 (and_17_out, not_25_out, not_26_out, not_27_out);
  not not_26 (not_26_out, C);
  not not_27 (not_27_out, B);
  not not_28 (not_28_out, C);
  and and_18 (and_18_out, not_28_out, not_29_out);
  not not_29 (not_29_out, A);
  and and_19 (and_19_out, B, not_30_out);
  not not_30 (not_30_out, A);
  and and_20 (and_20_out, D, B);
  and and_21 (and_21_out, D, C);
  not not_31 (not_31_out, B);
  and and_22 (and_22_out, C, not_32_out);
  not not_32 (not_32_out, A);
  not not_33 (not_33_out, C);
  and and_23 (and_23_out, not_33_out, B);
  and and_24 (and_24_out, C, not_34_out);
  not not_34 (not_34_out, B);
  and and_25 (and_25_out, C, not_35_out);
  not not_35 (not_35_out, A);
  or or_1 (a_2, and_1_out, and_2_out, and_3_out, D);
  or or_2 (b_2, and_4_out, and_5_out, and_6_out, and_7_out);
  or or_3 (c_2, and_8_out, and_9_out, and_10_out, and_11_out);
  or or_4 (d_2, and_12_out, and_13_out, and_14_out, and_15_out, and_16_out);
  or or_5 (e, and_17_out, and_18_out, and_19_out, and_20_out, and_21_out);
  or or_6 (f, not_31_out, and_22_out, D);
  or or_7 (g, and_23_out, and_24_out, and_25_out, D);

  // Notes on the sheet:
  //   7 segment PLD
  //   Ahmad Mohammad
  //   09/24
endmodule
